# Fritzing sketch circuitSchema (saved by Fritzing 0.9.3b)
breadboards: 1

parts:
  Reset = Pushbutton [package="[THT]"]
  R1 = Resistor [tolerance=±5% resistance=220 package=THT]
  Part2 = Arduino Uno (Rev3)
  White_sensor = LHi958 [package=to-39]
  Y_- = Pushbutton [package="[THT]"]
  R2 = Resistor [tolerance=±5% resistance=220 package=THT]
  Y_+ = Pushbutton [package="[THT]"]
  R3 = Resistor [tolerance=±5% resistance=220 package=THT]
  W_- = Pushbutton [package="[THT]"]
  R4 = Resistor [tolerance=±5% resistance=220 package=THT]
  W_+ = Pushbutton [package="[THT]"]
  R5 = Resistor [tolerance=±5% resistance=220 package=THT]
  R6 = Resistor [tolerance=±5% resistance=220 package=THT]
  Lights = Pushbutton [package="[THT]"]
  Yellow_sensor = LHi958 [package=to-39]
  WS2813_strip = ws2812b [package="smd 2812b"]
  Buzzer = Piezo Speaker

nets:
  5V: Reset.Pin_1, Reset.Pin_2, Part2.5V, White_sensor.n.a., Y_-.Pin_1, Y_-.Pin_2, Y_+.Pin_3, Y_+.Pin_4, W_-.Pin_1, W_-.Pin_2, W_+.Pin_3, W_+.Pin_4, Lights.Pin_1, Lights.Pin_2, Yellow_sensor.n.a., WS2813_strip.VDD
  N1: Reset.Pin_3, Reset.Pin_4, R1.Pin_1, Part2.RESET
  GND: R1.Pin_0, Part2.GND, White_sensor.GND, R2.Pin_0, R3.Pin_1, R4.Pin_0, R5.Pin_1, R6.Pin_0, Yellow_sensor.GND, WS2813_strip.VSS, Buzzer.pin1
  N2: Part2.D8, Yellow_sensor.D
  N3: Part2.D9_PWM, WS2813_strip.DIN
  N4: Part2.D10_PWM/SS, Buzzer.pin2
  N5: Part2.D2, Y_-.Pin_3, Y_-.Pin_4, R2.Pin_1
  N6: Part2.D3_PWM, Y_+.Pin_1, Y_+.Pin_2, R3.Pin_0
  N7: Part2.D4, W_-.Pin_3, W_-.Pin_4, R4.Pin_1
  N8: Part2.D5_PWM, W_+.Pin_1, W_+.Pin_2, R5.Pin_0
  N9: Part2.D6_PWM, R6.Pin_1, Lights.Pin_3, Lights.Pin_4
  N10: Part2.D7, White_sensor.D
